# Fritzing sketch Pullman (saved by Fritzing 0.9.3b)
breadboards: 1

parts:
  Часть1 = Arduino Nano (Rev3.0)
  M3 = DC Motor
  L298N1 = L298_BRIDGE_DRIVER [package=powerso20]
  M4 = DC Motor
  M5 = DC Motor
  U1 = DC-DC_CONVERTER [package=dc-dc_converter]
  LED1 = smd LED [color="Red (633nm)" package="0603 [SMD]"]
  LED2 = smd LED [color="Green (570nm)" package="0805 [SMD]"]
  R1 = Resistor [tolerance=±5% resistance=100k package="0805 [SMD]"]
  R2 = Resistor [tolerance=±5% resistance=10k package="0805 [SMD]"]
  Q1 = Basic FET N-Channel [package="TO220 [THT]"]
  R3 = Resistor [tolerance=±5% resistance=10k package=THT]
  R4 = Resistor [tolerance=±5% resistance=100 package=THT]
  D1 = Rectifier Diode [part_number=1N4001 package="Melf DO-213 AB [SMD]"]
  D1_2 = Rectifier Diode [part_number=1N4007 package="300 mil [THT]"]
  V9 = DC Power [voltage=14.4]

nets:
  GND: Часть1.GND, L298N1.GND, R2.Pin_1
  N1: Часть1.D2, LED2.cathode
  N2: Часть1.D3, R4.Pin_0
  N3: Часть1.D4, L298N1.IN4
  N4: Часть1.D5, LED1.cathode
  N5: Часть1.D6, L298N1.IN3
  N6: Часть1.D7, L298N1.IN2
  N7: Часть1.D8, L298N1.IN1
  N8: Часть1.D9, L298N1.ENA
  N9: Часть1.D10, L298N1.ENB
  5V: Часть1.5V, L298N1.VS, U1.VOUT
  N10: Часть1.A0, R1.Pin_1, R2.Pin_0
  14.4V: M3.pin_1, L298N1.VSS, U1.VIN, R1.Pin_0, D1.cathode, D1_2.cathode, V9.V+
  N11: M3.pin_2, Q1.drain, D1.anode, D1_2.anode
  N12: L298N1.NC, L298N1.OUT1, L298N1.OUT4, M4.pin_2, M5.pin_1
  N13: L298N1.OUT2, M5.pin_2
  N14: L298N1.OUT3, M4.pin_1
  GND_2: U1.GND1, U1.GND2, LED1.anode, LED2.anode, Q1.source, R3.Pin_1, V9.V-
  N15: Q1.gate, R3.Pin_0, R4.Pin_1
